// Logisim project teamsqlogIc.circ as structural Verilog: 1 circuit, main circuit main
module main (
  input  J,
  input  K,
  input  J2,
  input  K2,
  input  J3,
  input  K3,
  input  L,
  output X,
  output X2,
  output X3
);

  wire and_1_out, not_1_out, not_2_out;

  not not_1 (not_1_out, L);
  not not_2 (not_2_out, K2);
  and and_1 (and_1_out, K3, not_1_out);
  or or_1 (X, J, K);
  and and_2 (X2, J2, not_2_out);
  and and_3 (X3, J3, and_1_out);

  // Notes on the sheet:
  //   Question 2
  //   Question 3
  //   Question !
endmodule
